# Fritzing sketch circuit_diagram (saved by Fritzing 0.9.5d)
breadboards: 1

parts:
  J1 = DHT22 temperature-humidity sensor [form="♂ (male)" package=THT]
  U1 = NodeMCU V3.0
  R1 = Resistor [tolerance=±5% resistance=10k package=THT]
  Part1 = FC-28 Soil Hygrometer Module
  Part2 = FC-28 Soil Hygrometer Module - Probe
  Mini_Water_Pump_3-6VDC1 = Mini Water Pump 3-6VDC [part_number="Mini Water Pump 3-6VDC" chip_label=IC package="DIP (Dual Inline) [THT]"]
  KY-1 = Keyes Relay [package=THT]
  Water_Level_Sensor1 = LIQUID SENSING: Water Level Sensor [part_number="Water Level Sensor" chip_label=IC package="DIP (Dual Inline) [THT]"]
  LCM1602_IIC1 = LCM1602 IIC [part_number="LCM1602 IIC" chip_label="LCM1602 IIC" package="DIP (Dual Inline) [THT]"]
  LCD1 = LCD screen

nets:
  VCC: J1.VCC, U1.3V3, R1.Pin_0, Part1.VCC, KY-1.power, KY-1.C, Water_Level_Sensor1.VCC, LCM1602_IIC1.VCC
  N1: J1.OUT, U1.D2, R1.Pin_1
  GND: J1.GND, U1.GND, Part1.GND, Mini_Water_Pump_3-6VDC1.-M, KY-1.ground, Water_Level_Sensor1.GND, LCM1602_IIC1.GND
  N2: U1.D1, LCM1602_IIC1.SCL
  N3: U1.D3, LCM1602_IIC1.SDA
  N4: U1.D5, KY-1.signal
  N5: U1.A0, Part1.AO, Water_Level_Sensor1.OUT1
  N6: Part1.POS, Part2.POS
  N7: Part1.NEG, Part2.NEG
  N8: Mini_Water_Pump_3-6VDC1.+M, KY-1.NO
  VSS: LCM1602_IIC1.VSS, LCD1.VSS
  VDD: LCM1602_IIC1.VDD, LCD1.VDD
  N9: LCM1602_IIC1.V0, LCD1.V0
  N10: LCM1602_IIC1.RS, LCD1.RS
  N11: LCM1602_IIC1.RW, LCD1.R/W
  N12: LCM1602_IIC1.E, LCD1.E
  N13: LCM1602_IIC1.D0, LCD1.DB0
  N14: LCM1602_IIC1.D1, LCD1.DB1
  N15: LCM1602_IIC1.D2, LCD1.DB2
  N16: LCM1602_IIC1.D3, LCD1.DB3
  N17: LCM1602_IIC1.D4, LCD1.DB4
  N18: LCM1602_IIC1.D5, LCD1.DB5
  N19: LCM1602_IIC1.D6, LCD1.DB6
  N20: LCM1602_IIC1.D7, LCD1.DB7
  N21: LCM1602_IIC1.A, LCD1.LED+
  N22: LCM1602_IIC1.K, LCD1.LED-
  N23: LCM1602_IIC1.LED_A, LCM1602_IIC1.LED_B

custom parts:
  DHT22 temperature-humidity sensor: The DHT22 is a basic, low-cost digital temperature and humidity sensor. It uses a capacitive humidity sensor and a thermistor to measure the surrounding air, and spits out a digital signal on the data pin (no analog input pins needed). It's fairly simple to use, but requires careful timing to grab data. The only real downside of this sensor is you can only get new data from it once every 2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
  NodeMCU V3.0: NodeMcu V3 Lua WIFI Development Board
  FC-28 Soil Hygrometer Module: The FC-28 is a soil hygrometer module that uses the Texas Instruments LM393 comparator chip to provide an analog measurement of soil humidity. The digital output is high when soil moisture is over a certain threshold, as determined by adjusting the potentiometer.
  FC-28 Soil Hygrometer Module - Probe: The FC-28 is a soil hygrometer module that uses the Texas Instruments LM393 comparator chip to provide an analog measurement of soil humidity.
  Keyes Relay: The Keyes 5V relay module is suitable for SCM development, home appliance control. It uses a 5V~12V TIL control signal which can control DC / AC signal.
  LIQUID SENSING: Water Level Sensor: The new water level indicator with sturdy stainless steel probe also for detecting the level of water. With its simple 3-LED status indicator, and gives out a digital output. Compatible in all gizDuino boards. Input supply +5VDC.
  LCM1602 IIC: I2C-Module to use a 1602 or 2004 LCD on with the wire.h libory Serial LCD Modul
